// Logisim project Cache - Copy.circ as structural Verilog: 3 circuits, main circuit implementation
module implementation (
  input  [9:0] CpuAddressIn,
  input  CpuReadIn,
  input  CpuWriteIn,
  input  [7:0] CpuWriteValueIn,
  input  [31:0] LineFromMemIn,
  input  ClkIn,
  output ReadyOut,
  output DidContainOut,
  output [7:0] ByteReadOut,
  output [7:0] MemAddressOut,
  output MemReadOut,
  output MemWriteOut,
  output [31:0] Line2MemOut
);

  wire ContainsOut, set_1_containout, set_2_containout;

  Set set_1 (.ContainOut(set_1_containout));  // open: CPUTag, Offset, Data, ReadIn, WriteIn
  Set set_2 (.ContainOut(set_2_containout));  // open: CPUTag, Offset, Data, ReadIn, WriteIn
  Multiplexer #(.enable("false")) multiplexer_1 (
    .in0(set_1_containout), .in1(set_2_containout), .out(ContainsOut), .sel(CpuAddressIn[2]));

  // Other names for the same wires on the sheet: clk = ClkIn; CpuAddress[9:0] = CpuAddressIn;
  //   Offset[1:0] = CpuAddressIn[1:0]; Set = CpuAddressIn[2]; CPUTag[6:0] = CpuAddressIn[9:3]; CpuRead = CpuReadIn;
  //   CpuWrite = CpuWriteIn; CpuWriteValue[7:0] = CpuWriteValueIn; DidContain = DidContainOut;
  //   LineFromMem[31:0] = LineFromMemIn; MemAddress[7:0] = MemAddressOut; MemRead = MemReadOut;
  //   MemWrite = MemWriteOut; Ready = ReadyOut; ByteRead[7:0] = ByteReadOut; SelectedSetByteRead[7:0] = ByteReadOut;
  //   Line2Mem[31:0] = Line2MemOut; SelectedSetLine2Mem[31:0] = Line2MemOut
endmodule

module Set (
  input  [6:0] CPUTag,
  input  [1:0] Offset,
  input  [31:0] Data,
  input  ReadIn,
  input  WriteIn,
  output ContainOut
);

  Way way_1 ();  // open: AgeIn, ReadIn, WriteIn, CPUTag, BlockIn, ByteIn, OffsetIn, AgeOut, ValidOut, DirtyOut, TagOut, ContainsOut, BlockOut, ByteOut
  Way way_2 ();  // open: AgeIn, ReadIn, WriteIn, CPUTag, BlockIn, ByteIn, OffsetIn, AgeOut, ValidOut, DirtyOut, TagOut, ContainsOut, BlockOut, ByteOut
  Way way_3 ();  // open: AgeIn, ReadIn, WriteIn, CPUTag, BlockIn, ByteIn, OffsetIn, AgeOut, ValidOut, DirtyOut, TagOut, ContainsOut, BlockOut, ByteOut
  // OR_Gate or_1 has open pins: out=ContainOut
endmodule

module Way (
  input  [1:0] AgeIn,
  input  ReadIn,
  input  WriteIn,
  input  [6:0] CPUTag,
  input  [31:0] BlockIn,
  input  [7:0] ByteIn,
  input  [1:0] OffsetIn,
  output [1:0] AgeOut,
  output ValidOut,
  output DirtyOut,
  output [6:0] TagOut,
  output ContainsOut,
  output [31:0] BlockOut,
  output [7:0] ByteOut
);

  wire Byte0Write, Byte1Write, Byte2Write, Byte3Write, comparator_1_eq, or_1_out;
  wire [7:0] multiplexer_1_out, multiplexer_2_out, multiplexer_3_out, multiplexer_4_out;

  Multiplexer #(.enable("false"), .width(8)) multiplexer_1 (
    .in0(ByteIn), .in1(BlockIn[31:24]), .out(multiplexer_1_out), .sel(ReadIn));
  Multiplexer #(.enable("false"), .width(8)) multiplexer_2 (
    .in0(ByteIn), .in1(BlockIn[7:0]), .out(multiplexer_2_out), .sel(ReadIn));
  Multiplexer #(.enable("false"), .width(8)) multiplexer_3 (
    .in0(ByteIn), .in1(BlockIn[15:8]), .out(multiplexer_3_out), .sel(ReadIn));
  Multiplexer #(.enable("false"), .width(8)) multiplexer_4 (
    .in0(ByteIn), .in1(BlockIn[23:16]), .out(multiplexer_4_out), .sel(ReadIn));
  Register #(.width(2)) register_1 (.D(AgeIn), .clk(or_1_out), .Q(AgeOut));  // open: en, clr
  or or_1 (or_1_out, ReadIn, WriteIn);
  Register #(.width(7)) Tag (.Q(TagOut));  // open: D, en, clk, clr
  Register Byte0 (.D(multiplexer_2_out), .en(Byte0Write), .Q(BlockOut[7:0]));  // open: clk, clr
  Register Byte1 (.D(multiplexer_3_out), .en(Byte1Write), .Q(BlockOut[15:8]));  // open: clk, clr
  Register Byte2 (.D(multiplexer_4_out), .en(Byte2Write), .Q(BlockOut[23:16]));  // open: clk, clr
  Register Byte3 (.D(multiplexer_1_out), .en(Byte3Write), .Q(BlockOut[31:24]));  // open: clk, clr
  Comparator #(.width(7)) comparator_1 (.a(CPUTag), .b(TagOut), .eq(comparator_1_eq));  // open: gt, lt
  Register #(.width(1)) Valid (.Q(ValidOut));  // open: D, en, clk, clr
  and and_1 (ContainsOut, comparator_1_eq, ValidOut);
  Register #(.width(1)) register_2 (.D(1'b1), .clk(WriteIn), .Q(DirtyOut), .clr(ReadIn));  // open: en
  Multiplexer #(.enable("false"), .select(2), .width(8)) multiplexer_5 (
    .in0(BlockOut[7:0]), .in1(BlockOut[15:8]), .in2(BlockOut[23:16]), .in3(BlockOut[31:24]), .out(ByteOut),
    .sel(OffsetIn));

  // Other names for the same wires on the sheet: Byte0Out[7:0] = BlockOut[7:0]; Byte1Out[7:0] = BlockOut[15:8];
  //   Byte2Out[7:0] = BlockOut[23:16]; Byte3Out[7:0] = BlockOut[31:24]

  // Notes on the sheet:
  //   Whenever Write happens, Dirty becomes 1
endmodule
