// Logisim project Cachebkcup.circ as structural Verilog: 6 circuits, main circuit implementation
module implementation (
  input  [9:0] CpuAddressIn,
  input  CpuReadIn,
  input  CpuWriteIn,
  input  [7:0] CpuWriteValueIn,
  input  [31:0] LineFromMemIn,
  input  ClkIn,
  output ReadyOut,
  output DidContainOut,
  output [7:0] ByteReadOut,
  output [7:0] MemAddressOut,
  output MemReadOut,
  output MemWriteOut,
  output [31:0] Line2MemOut
);

  wire Contains0out, Contains1out, ContainsOut, CpuReadSaved, CpuWriteSaved, Dirty0out, Dirty1out,
       StartCache, UpdateAge, UpdateAge0, UpdateAge1;
  wire [3:0] nextstatefsm_1_stateout, register_5_q;
  wire [7:0] Byte0Out, Byte1Out, ByteIn;
  wire [31:0] Block0Out, Block1Out;

  Register #(.width(1)) register_1 (.D(CpuReadIn), .clk(ClkIn), .Q(CpuReadSaved));  // open: en, clr
  Register #(.width(1)) register_2 (.D(CpuWriteIn), .clk(ClkIn), .Q(CpuWriteSaved));  // open: en, clr
  Register register_3 (.D(CpuWriteValueIn), .clk(ClkIn), .Q(ByteIn));  // open: en, clr
  Decoder decoder_1 (.out0(UpdateAge0), .out1(UpdateAge1), .sel(CpuAddressIn[2]), .en(UpdateAge));
  Set set_1 (
    .CPUTag(CpuAddressIn[9:3]), .ByteIn(ByteIn), .Offset(CpuAddressIn[1:0]), .Data(LineFromMemIn),
    .ReadIn(CpuReadSaved), .WriteIn(CpuWriteSaved), .UpdateAges(UpdateAge0), .ClkIn(ClkIn),
    .ByteOut(Byte0Out), .BlockOut(Block0Out), .DirtyOut(Dirty0out), .ContainOut(Contains0out));
  Set set_2 (
    .CPUTag(CpuAddressIn[9:3]), .ByteIn(ByteIn), .Offset(CpuAddressIn[1:0]), .Data(LineFromMemIn),
    .ReadIn(CpuReadSaved), .WriteIn(CpuWriteSaved), .UpdateAges(UpdateAge1), .ClkIn(ClkIn),
    .ByteOut(Byte1Out), .BlockOut(Block1Out), .DirtyOut(Dirty1out), .ContainOut(Contains1out));
  Register #(.width(1)) u_StartCache (.D(1'b1), .clk(ClkIn), .Q(StartCache));  // open: en, clr
  Multiplexer #(.enable("false")) multiplexer_1 (
    .in0(Contains0out), .in1(Contains1out), .out(ContainsOut), .sel(CpuAddressIn[2]));
  Multiplexer #(.enable("false")) multiplexer_2 (
    .in0(Dirty0out), .in1(Dirty1out), .out(MemWriteOut), .sel(CpuAddressIn[2]));
  NextstateFSM nextstatefsm_1 (
    .Readin(CpuReadSaved), .Writein(CpuWriteSaved), .Dirtyin(MemWriteOut), .Memread(MemReadOut),
    .Memwrite(MemWriteOut), .Didcontain(ContainsOut), .ReadyCache(StartCache),
    .StateOut(nextstatefsm_1_stateout));
  Register #(.width(1)) register_4 (.D(MemReadOut), .clk(ClkIn), .clr(ContainsOut));  // open: en, Q
  and and_1 (MemReadOut, ~ContainsOut, CpuReadIn);  // AND_Gate
  Register #(.width(4)) register_5 (.D(nextstatefsm_1_stateout), .clk(ClkIn), .Q(register_5_q));  // open: en, clr
  Multiplexer #(.enable("false"), .width(32)) multiplexer_3 (
    .in0(Block0Out), .in1(Block1Out), .out(Line2MemOut), .sel(CpuAddressIn[2]));
  Multiplexer #(.enable("false"), .width(8)) multiplexer_4 (
    .in0(Byte0Out), .in1(Byte1Out), .out(ByteReadOut), .sel(CpuAddressIn[2]));
  outputFSM outputfsm_1 (.Input1(register_5_q), .UpdateAge(UpdateAge), .Ready(ReadyOut));

  assign MemAddressOut = {CpuAddressIn[2], CpuAddressIn[9:3]};

  // Other names for the same wires on the sheet: clk = ClkIn; CpuAddress[9:0] = CpuAddressIn;
  //   Offset[1:0] = CpuAddressIn[1:0]; CpuRead = CpuReadIn; CpuWrite = CpuWriteIn;
  //   CpuWriteValue[7:0] = CpuWriteValueIn; DidContain = DidContainOut; LineFromMem[31:0] = LineFromMemIn;
  //   CPUTag[6:0] = CpuAddressIn[9:3]; MemAddress[7:0] = {CpuAddressIn[2], CpuAddressIn[9:3]};
  //   ReadThisSet = CpuAddressIn[2]; MemRead = MemReadOut; IsDirty = MemWriteOut; MemWrite = MemWriteOut;
  //   Ready = ReadyOut; ByteRead[7:0] = ByteReadOut; SelectedSetByteRead[7:0] = ByteReadOut;
  //   Line2Mem[31:0] = Line2MemOut; SelectedSetLine2Mem[31:0] = Line2MemOut
endmodule

module Set (
  input  [6:0] CPUTag,
  input  [7:0] ByteIn,
  input  [1:0] Offset,
  input  [31:0] Data,
  input  ReadIn,
  input  WriteIn,
  input  UpdateAges,
  input  ClkIn,
  output [7:0] ByteOut,
  output [31:0] BlockOut,
  output DirtyOut,
  output ContainOut
);

  wire comparator_1_eq, comparator_2_eq, comparator_3_eq, Dirty0, Dirty1, Dirty2, InitializeAge, Read0,
       Read1, Read2, register_1_q, Tag0Contains, Tag1Contains, Tag2Contains, Valid0, Valid1, Valid2,
       WriteIn0, WriteIn1, WriteIn2;
  wire [1:0] AgeAccessed, CurrentAge, multiplexer_1_out, multiplexer_2_out, Way0Age, Way1Age, Way2Age,
       WayToEvict;
  wire [6:0] TagOut0, TagOut1, TagOut2;
  wire [7:0] ByteOut0, ByteOut1, ByteOut2;
  wire [31:0] BlockOut0, BlockOut1, BlockOut2;

  Register #(.width(1)) register_1 (.D(1'b1), .clk(ClkIn), .Q(register_1_q));  // open: en, clr
  Demultiplexer #(.enable("false"), .select(2)) demultiplexer_1 (
    .out0(WriteIn0), .out1(WriteIn1), .out2(WriteIn2), .in(WriteIn), .sel(Offset));  // open: out3
  Demultiplexer #(.enable("false"), .select(2)) demultiplexer_2 (
    .out0(Read0), .out1(Read1), .out2(Read2), .in(ReadIn), .sel(Offset));  // open: out3
  not not_1 (InitializeAge, register_1_q);
  Multiplexer #(.enable("false"), .width(2)) multiplexer_1 (
    .in0(WayToEvict), .in1({Tag2Contains, Tag1Contains}), .out(multiplexer_1_out), .sel(ContainOut));
  Register #(.width(2)) register_2 (.D(multiplexer_2_out), .clk(UpdateAges), .Q(CurrentAge));  // open: en, clr
  Multiplexer #(.enable("false"), .select(2), .width(2)) multiplexer_2 (
    .in0(Way0Age), .in1(Way1Age), .in2(Way2Age), .out(multiplexer_2_out), .sel(multiplexer_1_out));  // open: in3
  Way way_1 (
    .ReadIn(Read0), .WriteIn(WriteIn0), .CPUTag(CPUTag), .ByteIn(ByteIn), .OffsetIn(Offset), .ClkIn(ClkIn),
    .DataIn(Data), .ValidOut(Valid0), .DirtyOut(Dirty0), .TagOut(TagOut0), .BlockOut(BlockOut0),
    .ByteOut(ByteOut0));
  Way way_2 (
    .ReadIn(Read1), .WriteIn(WriteIn1), .CPUTag(CPUTag), .ByteIn(ByteIn), .OffsetIn(Offset), .ClkIn(ClkIn),
    .DataIn(Data), .ValidOut(Valid1), .DirtyOut(Dirty1), .TagOut(TagOut1), .BlockOut(BlockOut1),
    .ByteOut(ByteOut1));
  Way way_3 (
    .ReadIn(Read2), .WriteIn(WriteIn2), .CPUTag(CPUTag), .ByteIn(ByteIn), .OffsetIn(Offset), .ClkIn(ClkIn),
    .DataIn(Data), .ValidOut(Valid2), .DirtyOut(Dirty2), .TagOut(TagOut2), .BlockOut(BlockOut2),
    .ByteOut(ByteOut2));
  Ages ages_1 (
    .AgeAccessed(AgeAccessed), .UpdateAge(UpdateAges), .Initialize(InitializeAge), .ClkIn(ClkIn),
    .Way0Age(Way0Age), .Way1Age(Way1Age), .Way2Age(Way2Age), .WayToEvict(WayToEvict));
  Comparator #(.mode("unsigned"), .width(7)) comparator_1 (
    .a(CPUTag), .b(TagOut0), .eq(comparator_1_eq));  // open: gt, lt
  Comparator #(.mode("unsigned"), .width(7)) comparator_2 (
    .a(CPUTag), .b(TagOut1), .eq(comparator_2_eq));  // open: gt, lt
  Comparator #(.mode("unsigned"), .width(7)) comparator_3 (
    .a(CPUTag), .b(TagOut2), .eq(comparator_3_eq));  // open: gt, lt
  Multiplexer #(.enable("false"), .select(2)) multiplexer_3 (
    .in0(Dirty0), .in1(Dirty1), .in2(Dirty2), .out(DirtyOut), .sel(WayToEvict));  // open: in3
  and and_1 (Tag0Contains, comparator_1_eq, Valid0);
  and and_2 (Tag1Contains, comparator_2_eq, Valid1);
  and and_3 (Tag2Contains, comparator_3_eq, Valid2);
  or or_1 (ContainOut, Tag0Contains, Tag1Contains, Tag2Contains);

  // Other names for the same wires on the sheet: clk = ClkIn
endmodule

module Way (
  input  ReadIn,
  input  WriteIn,
  input  [6:0] CPUTag,
  input  [7:0] ByteIn,
  input  [1:0] OffsetIn,
  input  ClkIn,
  input  [31:0] DataIn,
  output ValidOut,
  output DirtyOut,
  output [6:0] TagOut,
  output [31:0] BlockOut,
  output [7:0] ByteOut
);

  wire Byte0Write, Byte1Write, Byte2Write, Byte3Write, ChangeBytes, demultiplexer_1_out0,
       demultiplexer_1_out1, demultiplexer_1_out2, demultiplexer_1_out3;
  wire [7:0] multiplexer_1_out, multiplexer_2_out, multiplexer_3_out, multiplexer_4_out;

  or or_1 (ChangeBytes, ReadIn, WriteIn);
  Multiplexer #(.enable("false"), .width(8)) multiplexer_1 (
    .in0(ByteIn), .in1(DataIn[31:24]), .out(multiplexer_1_out), .sel(ReadIn));
  Multiplexer #(.enable("false"), .width(8)) multiplexer_2 (
    .in0(ByteIn), .in1(DataIn[7:0]), .out(multiplexer_2_out), .sel(ReadIn));
  Multiplexer #(.enable("false"), .width(8)) multiplexer_3 (
    .in0(ByteIn), .in1(DataIn[15:8]), .out(multiplexer_3_out), .sel(ReadIn));
  Multiplexer #(.enable("false"), .width(8)) multiplexer_4 (
    .in0(ByteIn), .in1(DataIn[23:16]), .out(multiplexer_4_out), .sel(ReadIn));
  Register Byte0 (.D(multiplexer_2_out), .en(Byte0Write), .clk(ClkIn), .Q(BlockOut[7:0]));  // open: clr
  Register Byte1 (.D(multiplexer_3_out), .en(Byte1Write), .clk(ClkIn), .Q(BlockOut[15:8]));  // open: clr
  Register Byte2 (.D(multiplexer_4_out), .en(Byte2Write), .clk(ClkIn), .Q(BlockOut[23:16]));  // open: clr
  Register Byte3 (.D(multiplexer_1_out), .en(Byte3Write), .clk(ClkIn), .Q(BlockOut[31:24]));  // open: clr
  Demultiplexer #(.enable("false"), .select(2)) demultiplexer_1 (
    .out0(demultiplexer_1_out0), .out1(demultiplexer_1_out1), .out2(demultiplexer_1_out2),
    .out3(demultiplexer_1_out3), .in(ChangeBytes), .sel(OffsetIn));
  Register #(.width(1)) register_1 (.D(1'b1), .en(WriteIn), .clk(ClkIn), .Q(DirtyOut), .clr(ReadIn));
  or or_2 (Byte0Write, ReadIn, demultiplexer_1_out0);
  or or_3 (Byte1Write, ReadIn, demultiplexer_1_out1);
  or or_4 (Byte2Write, ReadIn, demultiplexer_1_out2);
  or or_5 (Byte3Write, ReadIn, demultiplexer_1_out3);
  Multiplexer #(.enable("false"), .select(2), .width(8)) multiplexer_5 (
    .in0(BlockOut[7:0]), .in1(BlockOut[15:8]), .in2(BlockOut[23:16]), .in3(BlockOut[31:24]), .out(ByteOut),
    .sel(OffsetIn));
  Register #(.width(1)) register_2 (.D(1'b1), .en(ChangeBytes), .clk(ClkIn), .Q(ValidOut));  // open: clr
  Register #(.width(7)) register_3 (.D(CPUTag), .en(ReadIn), .clk(ClkIn), .Q(TagOut));  // open: clr

  // Other names for the same wires on the sheet: BlockIn[31:0] = DataIn; Byte0Out[7:0] = BlockOut[7:0];
  //   Byte1Out[7:0] = BlockOut[15:8]; Byte2Out[7:0] = BlockOut[23:16]; Byte3Out[7:0] = BlockOut[31:24]; Clk = ClkIn

  // Notes on the sheet:
  //   Reading -> Putting into cache
  //   Writing -> Putting into memory
  //   Whenever Write happens, Dirty becomes 1
endmodule

module Ages (
  input  [1:0] AgeAccessed,
  input  UpdateAge,
  input  Initialize,
  input  ClkIn,
  output [1:0] Way0Age,
  output [1:0] Way1Age,
  output [1:0] Way2Age,
  output [1:0] WayToEvict
);

  wire comparator_4_gt, comparator_4_lt, comparator_5_gt, comparator_5_lt, comparator_6_gt, comparator_6_lt,
       UpdateAge_t;
  wire [1:0] adder_1_out, adder_2_out, adder_3_out, multiplexer_1_out, multiplexer_2_out, multiplexer_3_out,
       multiplexer_4_out, multiplexer_5_out, multiplexer_6_out;
  wire [2:0] and_1_out, comparator_1_gt, comparator_2_gt, comparator_3_gt;

  or or_1 (UpdateAge_t, UpdateAge, Initialize);
  Comparator #(.mode("unsigned"), .width(2)) comparator_1 (
    .a(Way0Age), .b(AgeAccessed), .gt(comparator_1_gt[0]), .eq(comparator_1_gt[1]), .lt(comparator_1_gt[2]));
  Adder #(.width(2)) adder_1 (.a(Way0Age), .b(2'b01), .out(adder_1_out));  // open: cin, cout
  Comparator #(.mode("unsigned"), .width(2)) comparator_2 (
    .a(Way1Age), .b(AgeAccessed), .gt(comparator_2_gt[0]), .eq(comparator_2_gt[1]), .lt(comparator_2_gt[2]));
  Adder #(.width(2)) adder_2 (.a(Way1Age), .b(2'b01), .out(adder_2_out));  // open: cin, cout
  Comparator #(.mode("unsigned"), .width(2)) comparator_3 (
    .a(Way2Age), .b(AgeAccessed), .gt(comparator_3_gt[0]), .eq(comparator_3_gt[1]), .lt(comparator_3_gt[2]));
  Adder #(.width(2)) adder_3 (.a(Way2Age), .b(2'b01), .out(adder_3_out));  // open: cin, cout
  Multiplexer #(.enable("false"), .select(3), .width(2)) multiplexer_1 (
    .in1(Way0Age), .in2(2'b00), .in4(adder_1_out), .out(multiplexer_1_out), .sel(comparator_1_gt));  // open: in0, in3, in5, in6, in7
  Multiplexer #(.enable("false"), .select(3), .width(2)) multiplexer_2 (
    .in1(Way1Age), .in2(2'b00), .in4(adder_2_out), .out(multiplexer_2_out), .sel(comparator_2_gt));  // open: in0, in3, in5, in6, in7
  Multiplexer #(.enable("false"), .select(3), .width(2)) multiplexer_3 (
    .in1(Way2Age), .in2(2'b00), .in4(adder_3_out), .out(multiplexer_3_out), .sel(comparator_3_gt));  // open: in0, in3, in5, in6, in7
  Comparator #(.width(2)) comparator_4 (
    .a(Way0Age), .b(Way1Age), .gt(comparator_4_gt), .lt(comparator_4_lt));  // open: eq
  Comparator #(.width(2)) comparator_5 (
    .a(Way0Age), .b(Way2Age), .gt(comparator_5_gt), .lt(comparator_5_lt));  // open: eq
  Comparator #(.width(2)) comparator_6 (
    .a(Way1Age), .b(Way2Age), .gt(comparator_6_gt), .lt(comparator_6_lt));  // open: eq
  Register #(.width(2)) register_1 (.D(multiplexer_4_out), .en(UpdateAge_t), .clk(ClkIn), .Q(Way0Age));  // open: clr
  Multiplexer #(.enable("false"), .width(2)) multiplexer_4 (
    .in0(multiplexer_1_out), .in1(2'b00), .out(multiplexer_4_out), .sel(Initialize));
  Register #(.width(2)) register_2 (.D(multiplexer_5_out), .en(UpdateAge_t), .clk(ClkIn), .Q(Way1Age));  // open: clr
  Multiplexer #(.enable("false"), .width(2)) multiplexer_5 (
    .in0(multiplexer_2_out), .in1(2'b01), .out(multiplexer_5_out), .sel(Initialize));
  Register #(.width(2)) register_3 (.D(multiplexer_6_out), .en(UpdateAge_t), .clk(ClkIn), .Q(Way2Age));  // open: clr
  Multiplexer #(.enable("false"), .width(2)) multiplexer_6 (
    .in0(multiplexer_3_out), .in1(2'b10), .out(multiplexer_6_out), .sel(Initialize));
  and and_1 (and_1_out[0], comparator_4_gt, comparator_5_gt);
  and and_2 (and_1_out[2], comparator_6_lt, comparator_5_lt);
  and and_3 (and_1_out[1], comparator_4_lt, comparator_6_gt);
  // Probe on Way0Age
  // Probe on Way1Age
  // Probe on Way2Age
  Multiplexer #(.enable("false"), .select(3), .width(2)) multiplexer_7 (
    .in0(2'b10), .in1(2'b00), .in2(2'b01), .in4(2'b10), .out(WayToEvict), .sel(and_1_out));  // open: in3, in5, in6, in7

  // Other names for the same wires on the sheet: clk = ClkIn; CurrentAge[1:0] = AgeAccessed
endmodule

module outputFSM (
  input  [3:0] Input1,
  output UpdateAge,
  output Ready
);

  wire and_1_out, and_2_out, not_1_out, not_2_out, not_3_out, not_4_out;

  not not_1 (not_1_out, Input1[3]);
  not not_2 (not_2_out, Input1[2]);
  not not_3 (not_3_out, Input1[1]);
  not not_4 (not_4_out, Input1[0]);
  and and_1 (and_1_out, not_2_out, not_3_out, Input1[0]);
  and and_2 (and_2_out, not_1_out, Input1[2], Input1[1], not_4_out);
  and and_3 (Ready, Input1[3], Input1[2], Input1[1], not_4_out);
  or or_1 (UpdateAge, and_1_out, and_2_out);
endmodule

module NextstateFSM (
  input  Readin,
  input  Writein,
  input  Dirtyin,
  input  Memread,
  input  Memwrite,
  input  Didcontain,
  input  ReadyCache,
  output [3:0] StateOut
);

  wire and_1_out, and_2_out, and_3_out, and_4_out, and_5_out, and_6_out, and_7_out, and_8_out, and_9_out,
       and_10_out, and_11_out, and_12_out, and_13_out, and_14_out, and_15_out, not_1_out, not_2_out,
       not_3_out, not_4_out, not_5_out, not_6_out, not_7_out;

  not not_1 (not_1_out, Readin);
  not not_2 (not_2_out, Writein);
  not not_3 (not_3_out, Dirtyin);
  not not_4 (not_4_out, Memread);
  not not_5 (not_5_out, Memwrite);
  not not_6 (not_6_out, Didcontain);
  not not_7 (not_7_out, ReadyCache);
  and and_1 (and_1_out, not_3_out, not_4_out, not_6_out, ReadyCache);
  and and_2 (and_2_out, not_2_out, Memread);
  and and_3 (and_3_out, Writein, not_4_out, not_6_out);
  and and_4 (and_4_out, not_1_out, not_2_out, not_3_out, not_4_out, not_5_out, not_6_out, ReadyCache);
  and and_5 (and_5_out, not_1_out, not_2_out, Memwrite, not_6_out, not_7_out);
  and and_6 (and_6_out, not_1_out, not_2_out, Memread, not_6_out, not_7_out);
  and and_7 (and_7_out, not_1_out, not_2_out, Dirtyin, not_6_out, not_7_out);
  and and_8 (and_8_out, Writein, Didcontain);
  and and_9 (and_9_out, not_1_out, not_2_out, not_3_out, not_4_out, not_5_out, not_6_out, ReadyCache);
  and and_10 (and_10_out, Writein, Memread);
  and and_11 (and_11_out, Writein, Dirtyin);
  and and_12 (and_12_out, not_4_out, Didcontain);
  and and_13 (and_13_out, Memwrite, ReadyCache);
  and and_14 (and_14_out, Memread, Memwrite);
  and and_15 (and_15_out, not_2_out, Dirtyin);
  or or_1 (StateOut[3], and_1_out, Memwrite, and_2_out, and_3_out, Readin);
  or or_2 (StateOut[2], and_4_out, and_5_out, and_6_out, and_7_out, and_8_out);
  or or_3 (StateOut[1], and_9_out, and_10_out, and_11_out);
  or or_4 (StateOut[0], and_12_out, and_13_out, and_14_out, and_15_out, Readin);
endmodule
