// Logisim project Cachegrader.circ as structural Verilog: 5 circuits, main circuit main
module main (
  input  StopOnMismatchIn,
  output MemReadOut,
  output ReadyOut,
  output DidContainOut,
  output CmdIsReadOut,
  output [7:0] ByteReadOut,
  output ClkOut,
  output halt
);

  wire CorrectValueWasReturnedOnRead, CPURead, CPUWrite, MaxIterationsReached, MemWrite, not_1_out, or_1_out,
       StopTesting;
  wire [3:0] IterationOfCurrentTest;
  wire [7:0] CPUWriteValue, MemAddress, SolutionByteRead;
  wire [9:0] CPUAddress, NumberOfCorrectReads, NumberOfHits, NumberOfMisses, TestNumber;
  wire [31:0] Line2Mem, LineFromMem;

  Clock clock_1 (.out(ClkOut));
  or or_1 (or_1_out, ReadyOut, MaxIterationsReached);
  not not_1 (not_1_out, ReadyOut);
  // Probe on CPURead
  // Probe on CPUWrite
  // Probe on CPUAddress
  // Probe on CPUWriteValue
  // Probe on LineFromMem
  Counter #(.max('h9), .width(4)) counter_1 (
    .load(ReadyOut), .up(not_1_out), .clk(ClkOut), .D(4'b0001), .carry(MaxIterationsReached),
    .Q(IterationOfCurrentTest));  // open: clr, count
  // Probe on TestNumber
  // Probe on IterationOfCurrentTest
  // Probe on NumberOfCorrectReads
  // Probe on NumberOfHits
  // Probe on NumberOfMisses
  InputGeneratorCirc inputgeneratorcirc_1 (
    .StopTestingIn(StopTesting), .GoToNextTestIn(or_1_out), .ClkIn(ClkOut), .DoneOut(halt),
    .ReadOut(CPURead), .WriteOut(CPUWrite), .AddressOut(CPUAddress), .ValueOut(CPUWriteValue),
    .TestNumberOut(TestNumber));
  // Probe on ReadyOut
  // Probe on DidContainOut
  // Probe on ByteReadOut
  // Probe on MemAddress
  // Probe on MemReadOut
  // Probe on MemWrite
  // Probe on Line2Mem
  // Probe on CmdIsReadOut
  // Probe on CorrectValueWasReturnedOnRead
  // Probe on SolutionByteRead
  implementation implementation_1 (
    .CpuAddressIn(CPUAddress), .CpuReadIn(CPURead), .CpuWriteIn(CPUWrite), .CpuWriteValueIn(CPUWriteValue),
    .LineFromMemIn(LineFromMem), .ClkIn(ClkOut), .ReadyOut(ReadyOut), .DidContainOut(DidContainOut),
    .ByteReadOut(ByteReadOut), .MemAddressOut(MemAddress), .MemReadOut(MemReadOut), .MemWriteOut(MemWrite),
    .Line2MemOut(Line2Mem));
  CheckerCirc checkercirc_1 (
    .StopOnIncorrect(StopOnMismatchIn), .TestNumberIn(TestNumber), .YourByteReadIn(ByteReadOut),
    .ReadyIn(ReadyOut), .ClkIn(ClkOut), .SolutionByteReadOut(SolutionByteRead),
    .CorrectValueWasReturnedOnReadOut(CorrectValueWasReturnedOnRead), .StopTestingOut(StopTesting),
    .CmdIsReadOut(CmdIsReadOut));
  StatsTracker statstracker_1 (
    .StopTestingIn(StopTesting), .DoneTestingIn(halt),
    .CorrectByteReturnedOnReadIn(CorrectValueWasReturnedOnRead), .ReadyIn(ReadyOut),
    .ContainedIn(DidContainOut), .MemReadIn(MemReadOut), .ClkIn(ClkOut),
    .NumberOfReadsCorrectOut(NumberOfCorrectReads), .NumberOfMissesOut(NumberOfMisses),
    .NumberOfHitsOut(NumberOfHits));
  RAM #(.asyncread("true"), .dataWidth(32)) ram_1 (
    .addr(MemAddress), .we(MemWrite), .oe(MemReadOut), .clk(ClkOut), .din(Line2Mem), .dout(LineFromMem));

  // Other names for the same wires on the sheet: ByteRead[7:0] = ByteReadOut; clk = ClkOut; CmdIsRead = CmdIsReadOut;
  //   DidContain = DidContainOut; MemRead = MemReadOut; Ready = ReadyOut; StopOnMismatch = StopOnMismatchIn;
  //   TestingFinsihed = halt

  // Notes on the sheet:
  //   Inputs
  //   Load The Inputs Into Here
  //   Once Max Iterations is Reached, 9, You are Forced to the Next Test
  //   Stats
  //   Outputs
  //   SetStepOnMismatch to 1 to have the testing circuit stop on the first READ that returns back the wrong value
  //   This Is Your Answer
  //   What Value Should Have Been Returned On A Read Command
  //   Values Here Only Matter When CmdIsRead == 1
  //   Place the Solution File Inside of This Circuit
  //   Load The Contents Of Memory Into Here
endmodule

module InputGeneratorCirc (
  input  StopTestingIn,
  input  GoToNextTestIn,
  input  ClkIn,
  output DoneOut,
  output ReadOut,
  output WriteOut,
  output [9:0] AddressOut,
  output [7:0] ValueOut,
  output [9:0] TestNumberOut
);

  wire and_1_out;

  and and_1 (and_1_out, GoToNextTestIn, ~StopTestingIn, ~DoneOut);  // AND_Gate
  Counter #(.max('h3ff), .width(10)) counter_1 (
    .up(1'b1), .count(and_1_out), .clk(ClkIn), .Q(TestNumberOut));  // open: clr, load, D, carry
  ROM #(.addrWidth(10), .dataWidth(21)) rom_1 (
    .addr(TestNumberOut), .data({DoneOut, ReadOut, WriteOut, AddressOut, ValueOut}));

  // Other names for the same wires on the sheet: Value[7:0] = ValueOut; Address[9:0] = AddressOut; Write = WriteOut;
  //   Read = ReadOut; Done = DoneOut; Clk = ClkIn; GoToNextTest = GoToNextTestIn; StopTesting = StopTestingIn;
  //   TestNumber[9:0] = TestNumberOut

  // Notes on the sheet:
  //   contents of rom_1 (hex, n*v repeats v):
  //   80000 80100 80200 80300 80400 80500 80600 80700 80800 80900 80a00 80b00 80c00 80d00 80e00 80f00
  //   81000 81100 81200 81300 81400 81500 81600 81700 0 100000
endmodule

module CheckerCirc (
  input  StopOnIncorrect,
  input  [9:0] TestNumberIn,
  input  [7:0] YourByteReadIn,
  input  ReadyIn,
  input  ClkIn,
  output [7:0] SolutionByteReadOut,
  output CorrectValueWasReturnedOnReadOut,
  output StopTestingOut,
  output CmdIsReadOut
);

  wire comparator_1_eq, not_1_out, or_1_out;
  wire [9:0] subtractor_1_out;

  not not_1 (not_1_out, ReadyIn);
  or or_1 (or_1_out, not_1_out, CorrectValueWasReturnedOnReadOut);
  ROM #(.addrWidth(10), .dataWidth(9)) rom_1 (.addr(subtractor_1_out), .data({CmdIsReadOut, SolutionByteReadOut}));
  Subtractor #(.width(10)) subtractor_1 (.a(TestNumberIn), .b(10'h1), .out(subtractor_1_out));  // open: bin, bout
  StopTestingCirc stoptestingcirc_1 (
    .StopOnIncorrectIn(StopOnIncorrect), .AnswerIsCorrectIn(or_1_out), .ClkIn(ClkIn),
    .StopTestingOut(StopTestingOut));
  Comparator comparator_1 (.a(SolutionByteReadOut), .b(YourByteReadIn), .eq(comparator_1_eq));  // open: gt, lt
  and and_1 (CorrectValueWasReturnedOnReadOut, ReadyIn, comparator_1_eq, CmdIsReadOut);

  // Other names for the same wires on the sheet: SolutionByteRead[7:0] = SolutionByteReadOut;
  //   CmdIsRead = CmdIsReadOut; Clk = ClkIn; CorrectValueWasReturnedOnRead = CorrectValueWasReturnedOnReadOut;
  //   Ready = ReadyIn; StopTesting = StopTestingOut; TestNumber[9:0] = TestNumberIn;
  //   YourByteRead[7:0] = YourByteReadIn

  // Notes on the sheet:
  //   contents of rom_1 (hex, n*v repeats v):
  //   100 101 102 103 104 105 106 107 108 109 10a 10b 10c 10d 10e 10f 110 111 112 113 114 115 116 117
  //   After Loading the test, right click the ROM and 
  //   Select Edit Contents To Make Sure It Was Loaded Correctly
endmodule

module StopTestingCirc (
  input  StopOnIncorrectIn,
  input  AnswerIsCorrectIn,
  input  ClkIn,
  output StopTestingOut
);

  wire SavedStopTesting, StopTesting;

  and and_1 (StopTesting, ~AnswerIsCorrectIn, StopOnIncorrectIn);  // AND_Gate
  Register #(.width(1)) register_1 (.D(StopTesting), .en(StopTesting), .clk(ClkIn), .Q(SavedStopTesting));  // open: clr
  or or_1 (StopTestingOut, StopTesting, SavedStopTesting);

  // Other names for the same wires on the sheet: AnswerIsCorrect = AnswerIsCorrectIn; clk = ClkIn;
  //   StopOnIncorrect = StopOnIncorrectIn
endmodule

module StatsTracker (
  input  StopTestingIn,
  input  DoneTestingIn,
  input  CorrectByteReturnedOnReadIn,
  input  ReadyIn,
  input  ContainedIn,
  input  MemReadIn,
  input  ClkIn,
  output [9:0] NumberOfReadsCorrectOut,
  output [9:0] NumberOfMissesOut,
  output [9:0] NumberOfHitsOut
);

  wire and_2_out, and_3_out, OkToCount;

  and and_1 (OkToCount, ~StopTestingIn, ~DoneTestingIn);  // AND_Gate
  and and_2 (and_2_out, CorrectByteReturnedOnReadIn, OkToCount);
  and and_3 (and_3_out, OkToCount, ReadyIn, ContainedIn);
  Counter #(.max('h3ff), .ongoal("stay"), .width(10)) counter_1 (
    .up(1'b1), .count(and_2_out), .clk(ClkIn), .Q(NumberOfReadsCorrectOut));  // open: clr, load, D, carry
  Counter #(.max('h3ff), .ongoal("stay"), .width(10)) counter_2 (
    .up(1'b1), .count(and_3_out), .clk(ClkIn), .Q(NumberOfHitsOut));  // open: clr, load, D, carry
  Counter #(.max('h3ff), .ongoal("stay"), .width(10)) counter_3 (
    .up(1'b1), .count(MemReadIn), .clk(ClkIn), .Q(NumberOfMissesOut));  // open: clr, load, D, carry

  // Other names for the same wires on the sheet: Clk = ClkIn; Contained = ContainedIn;
  //   CorrectByteReturnedOnRead = CorrectByteReturnedOnReadIn; DoneTesting = DoneTestingIn; MemRead = MemReadIn;
  //   NumberOfHits[9:0] = NumberOfHitsOut; NumberOfMisses[9:0] = NumberOfMissesOut;
  //   NumberOfReadsCorrect[9:0] = NumberOfReadsCorrectOut; Ready = ReadyIn; StopTesting = StopTestingIn
endmodule
