// Logisim project bcd.circ as structural Verilog: 1 circuit, main circuit implementation
module implementation (
  input  w3,
  input  w2,
  input  w1,
  input  w0,
  output a,
  output b,
  output c,
  output d,
  output e,
  output f,
  output g
);

  wire BD_out, BNC_out, BNCD_out, BND_out, CD_out, CND_out, NBC_out, NBND_out, NCND_out, not_1_out,
       not_2_out, not_3_out;

  not not_1 (not_1_out, w2);
  not not_2 (not_2_out, w1);
  not not_3 (not_3_out, w0);
  and NBND (NBND_out, not_1_out, not_3_out);
  and BD (BD_out, w2, w0);
  and BND (BND_out, w2, not_3_out);
  and CD (CD_out, w1, w0);
  and NCND (NCND_out, not_2_out, not_3_out);
  and CND (CND_out, w1, not_3_out);
  and BNCD (BNCD_out, w2, not_2_out, w0);
  and NBC (NBC_out, not_1_out, w1);
  and BNC (BNC_out, w2, not_2_out);
  or or_1 (a, w3, NBND_out, BD_out, w1);
  or or_2 (b, w3, not_1_out, CD_out, NCND_out);
  or or_3 (c, w2, w0, NCND_out);
  or or_4 (d, w3, NBND_out, CND_out, BNCD_out, NBC_out);
  or or_5 (e, CND_out, NBND_out);
  or or_6 (f, w3, BND_out, NCND_out, BNC_out);
  or or_7 (g, w3, CND_out, NBC_out, BNC_out);

  // Other names for the same wires on the sheet: at = a; bt = b; ct = c; dt = d; et = e; ft = f; gt = g; w0t = w0;
  //   w1t = w1; w2t = w2; w3t = w3
endmodule
