// Logisim project adder4.circ as structural Verilog: 1 circuit, main circuit implementation
module implementation (
  input  [3:0] Ain,
  input  [3:0] Bin,
  input  Cinin,
  output [3:0] Sum_Out,
  output Carry_Out
);

  wire and_1_out, and_2_out, and_3_out, and_4_out, and_5_out, and_6_out, and_7_out, and_8_out, and_9_out,
       and_10_out, c1, c2, c3_t, g0, g1, g2, g3, p0, p1, p2, p3;

  and u_g3 (g3, Ain[3], Bin[3]);
  xor u_p3 (p3, Ain[3], Bin[3]);
  and u_g2 (g2, Ain[2], Bin[2]);
  xor xor_1 (Sum_Out[3], p3, c3_t);
  xor u_p2 (p2, Ain[2], Bin[2]);
  xor xor_2 (Sum_Out[2], p2, c2);
  and u_g1 (g1, Ain[1], Bin[1]);
  xor u_p1 (p1, Ain[1], Bin[1]);
  xor xor_3 (Sum_Out[1], p1, c1);
  and u_g0 (g0, Ain[0], Bin[0]);
  xor u_p0 (p0, Ain[0], Bin[0]);
  xor xor_4 (Sum_Out[0], p0, Cinin);
  or or_1 (c1, g0, and_1_out);
  and and_1 (and_1_out, p0, Cinin);
  and and_2 (and_2_out, g0, p1);
  or or_2 (c2, g1, and_2_out, and_3_out);
  and and_3 (and_3_out, p0, p1, Cinin);
  and and_4 (and_4_out, g1, p2);
  or or_3 (c3_t, g2, and_4_out, and_5_out, and_6_out);
  and and_5 (and_5_out, g0, p1, p2);
  and and_6 (and_6_out, Cinin, p0, p1, p2);
  and and_7 (and_7_out, g2, p3);
  and and_8 (and_8_out, g1, p2, p3);
  or or_4 (Carry_Out, g3, and_7_out, and_8_out, and_9_out, and_10_out);
  and and_9 (and_9_out, g0, p1, p2, p3);
  and and_10 (and_10_out, Cinin, p0, p1, p2, p3);

  // Other names for the same wires on the sheet: A[3:0] = Ain; B[3:0] = Bin; C3 = Carry_Out; Cin = Cinin;
  //   Sum[3:0] = Sum_Out
endmodule
