// Logisim project bitcounter.circ as structural Verilog: 1 circuit, main circuit implementation
module implementation (
  input  [7:0] BitsIn,
  input  CountZerosIn,
  output [3:0] BitCountOut
);

  wire [1:0] adder_1_out, adder_2_out, adder_3_out, adder_4_out, adder_5_out, adder_6_out;
  wire [2:2] adder_5_cout, adder_6_cout;
  wire [3:0] ones, zeros;

  Adder #(.width(1)) adder_1 (.a(BitsIn[0]), .b(BitsIn[1]), .out(adder_1_out[0]), .cout(adder_1_out[1]));  // open: cin
  Adder #(.width(1)) adder_2 (.a(BitsIn[2]), .b(BitsIn[3]), .out(adder_2_out[0]), .cout(adder_2_out[1]));  // open: cin
  Adder #(.width(1)) adder_3 (.a(BitsIn[4]), .b(BitsIn[5]), .out(adder_3_out[0]), .cout(adder_3_out[1]));  // open: cin
  Adder #(.width(1)) adder_4 (.a(BitsIn[6]), .b(BitsIn[7]), .out(adder_4_out[0]), .cout(adder_4_out[1]));  // open: cin
  Adder #(.width(2)) adder_5 (
    .a(adder_1_out), .b(adder_2_out), .out(adder_5_out), .cout(adder_5_cout[2]));  // open: cin
  Adder #(.width(2)) adder_6 (
    .a(adder_3_out), .b(adder_4_out), .out(adder_6_out), .cout(adder_6_cout[2]));  // open: cin
  Multiplexer #(.enable("false"), .width(4)) multiplexer_1 (
    .in0(ones), .in1(zeros), .out(BitCountOut), .sel(CountZerosIn));
  Adder #(.width(3)) adder_7 (
    .a({adder_5_cout[2], adder_5_out}), .b({adder_6_cout[2], adder_6_out}), .out(ones[2:0]), .cout(ones[3]));  // open: cin
  Subtractor #(.width(4)) subtractor_1 (.a(4'b1000), .b(ones), .out(zeros));  // open: bin, bout

  // Other names for the same wires on the sheet: BitCount[3:0] = BitCountOut; Bits[7:0] = BitsIn;
  //   CountZeros = CountZerosIn
endmodule
