// Logisim project shifter.circ as structural Verilog: 1 circuit, main circuit implementation
module implementation (
  input  IsRightShiftIn,
  input  IsArithmeticIn,
  input  [1:0] ShiftAmountIn,
  input  [2:0] NumberIn,
  output [2:0] ShiftedNumberOut
);

  wire asr0, asr1, asr2, lr0, lr1, lr2, sl0, sl1, sl2;

  Multiplexer #(.enable("false"), .select(2)) multiplexer_1 (
    .in0(NumberIn[2]), .in1(NumberIn[1]), .in2(NumberIn[0]), .in3(1'b0), .out(sl2), .sel(ShiftAmountIn));
  Multiplexer #(.enable("false"), .select(2)) multiplexer_2 (
    .in0(NumberIn[1]), .in1(NumberIn[0]), .in2(1'b0), .in3(1'b0), .out(sl1), .sel(ShiftAmountIn));
  Multiplexer #(.enable("false"), .select(2)) multiplexer_3 (
    .in0(NumberIn[0]), .in1(1'b0), .in2(1'b0), .in3(1'b0), .out(sl0), .sel(ShiftAmountIn));
  Multiplexer #(.enable("false"), .select(2)) multiplexer_4 (
    .in0(NumberIn[2]), .in1(1'b0), .in2(1'b0), .in3(1'b0), .out(lr2), .sel(ShiftAmountIn));
  Multiplexer #(.enable("false"), .select(2)) multiplexer_5 (
    .in0(NumberIn[1]), .in1(NumberIn[2]), .in2(1'b0), .in3(1'b0), .out(lr1), .sel(ShiftAmountIn));
  Multiplexer #(.enable("false"), .select(2)) multiplexer_6 (
    .in0(NumberIn[0]), .in1(NumberIn[1]), .in2(NumberIn[2]), .in3(1'b0), .out(lr0), .sel(ShiftAmountIn));
  Multiplexer #(.enable("false"), .select(2), .width(3)) multiplexer_7 (
    .in0({sl2, sl1, sl0}), .in1({sl2, sl1, sl0}), .in2({lr2, lr1, lr0}), .in3({asr2, asr1, asr0}),
    .out(ShiftedNumberOut), .sel({IsRightShiftIn, IsArithmeticIn}));
  Multiplexer #(.enable("false"), .select(2)) multiplexer_8 (
    .in0(NumberIn[2]), .in1(NumberIn[2]), .in2(NumberIn[2]), .in3(NumberIn[2]), .out(asr2),
    .sel(ShiftAmountIn));
  Multiplexer #(.enable("false"), .select(2)) multiplexer_9 (
    .in0(NumberIn[1]), .in1(NumberIn[2]), .in2(NumberIn[2]), .in3(NumberIn[2]), .out(asr1),
    .sel(ShiftAmountIn));
  Multiplexer #(.enable("false"), .select(2)) multiplexer_10 (
    .in0(NumberIn[0]), .in1(NumberIn[1]), .in2(NumberIn[2]), .in3(NumberIn[2]), .out(asr0),
    .sel(ShiftAmountIn));

  // Other names for the same wires on the sheet: IsArithmetic = IsArithmeticIn; IsRightShift = IsRightShiftIn;
  //   Number[2:0] = NumberIn; ShiftAmount[1:0] = ShiftAmountIn; ShiftedNumber[2:0] = ShiftedNumberOut
endmodule
