// Logisim project FourBitParity.circ as structural Verilog
module implementation (
  input  EnableIn,
  input  InputBitIn,
  input  ClkIn,
  output IsEvenOut
);

  wire [2:0] register_1_q, state_1_outstate;

  // Probe on register_1_q
  // Probe on state_1_outstate
  Register #(.width(3)) register_1 (.D(state_1_outstate), .en(EnableIn), .clk(ClkIn), .Q(register_1_q));  // open: clr
  state state_1 (.state(register_1_q), .inval(InputBitIn), .outstate(state_1_outstate));
  and and_1 (IsEvenOut, 1'b1, 1'b1, 1'b1, register_1_q[2], register_1_q[1], register_1_q[0]);

  // Other names for the same wires on the sheet: Clk = ClkIn; Enable = EnableIn; InputBit = InputBitIn
endmodule

module state (
  input  [2:0] state,
  input  inval,
  output [2:0] outstate
);

  wire and_1_out, and_2_out, and_3_out, and_4_out, and_5_out, and_6_out, and_7_out, and_8_out, and_9_out,
       and_10_out, and_11_out, and_12_out, and_13_out, and_14_out, and_15_out, not_1_out, not_2_out,
       not_3_out, not_4_out;

  not not_1 (not_1_out, state[2]);
  not not_2 (not_2_out, state[1]);
  not not_3 (not_3_out, state[0]);
  not not_4 (not_4_out, inval);
  and and_1 (and_1_out, not_1_out, state[0], inval);
  and and_2 (and_2_out, not_1_out, state[1], not_4_out);
  and and_3 (and_3_out, state[2], not_2_out, not_3_out);
  and and_4 (and_4_out, state[2], not_3_out, not_4_out);
  and and_5 (and_5_out, state[2], not_2_out, inval);
  and and_6 (and_6_out, not_1_out, not_3_out, inval);
  and and_7 (and_7_out, not_2_out, not_3_out, inval);
  and and_8 (and_8_out, not_1_out, state[0], not_4_out);
  and and_9 (and_9_out, state[2], state[0], inval);
  and and_10 (and_10_out, state[2], state[1], not_3_out, not_4_out);
  and and_11 (and_11_out, not_1_out, not_2_out, not_4_out);
  and and_12 (and_12_out, not_2_out, not_3_out, not_4_out);
  and and_13 (and_13_out, not_1_out, state[1], inval);
  and and_14 (and_14_out, state[2], not_2_out, state[0], inval);
  and and_15 (and_15_out, state[2], state[1], not_4_out);
  or or_1 (outstate[2], and_1_out, and_2_out, and_3_out, and_4_out, and_5_out);
  or or_2 (outstate[1], and_6_out, and_7_out, and_8_out, and_9_out, and_10_out);
  or or_3 (outstate[0], and_11_out, and_12_out, and_13_out, and_14_out, and_15_out);
endmodule
