// Logisim project UpDownCounter.circ as structural Verilog: 2 circuits, main circuit implementation
module implementation (
  input  EnableIn,
  input  CountUpIn,
  input  CountDownIn,
  input  clkIn,
  output [2:0] Count
);

  wire [2:0] state_1_outstate;

  // Probe on Count
  Register #(.width(3)) register_1 (.D(state_1_outstate), .en(EnableIn), .clk(clkIn), .Q(Count));  // open: clr
  state state_1 (.state(Count), .upcount(CountUpIn), .downcount(CountDownIn), .outstate(state_1_outstate));

  // Other names for the same wires on the sheet: clk = clkIn; CountDown = CountDownIn; CountUp = CountUpIn;
  //   Enable = EnableIn
endmodule

module state (
  input  [2:0] state,
  input  upcount,
  input  downcount,
  output [2:0] outstate
);

  wire and_1_out, and_2_out, and_3_out, and_4_out, and_5_out, and_6_out, and_7_out, and_8_out, and_9_out,
       and_10_out, and_11_out, and_12_out, and_13_out, and_14_out, not_1_out, not_2_out, not_3_out, not_4_out;

  not not_1 (not_1_out, state[1]);
  not not_2 (not_2_out, state[0]);
  not not_3 (not_3_out, upcount);
  not not_4 (not_4_out, downcount);
  and and_1 (and_1_out, state[1], state[0], upcount, not_4_out);
  and and_2 (and_2_out, state[2], not_4_out);
  and and_3 (and_3_out, state[2], state[0]);
  and and_4 (and_4_out, state[2], state[1]);
  and and_5 (and_5_out, not_1_out, state[0], upcount, not_4_out);
  and and_6 (and_6_out, state[1], not_2_out, not_4_out);
  and and_7 (and_7_out, state[1], state[0], not_3_out);
  and and_8 (and_8_out, state[2], not_1_out, not_2_out, downcount);
  and and_9 (and_9_out, state[2], state[1], not_4_out);
  and and_10 (and_10_out, not_2_out, upcount);
  and and_11 (and_11_out, state[0], not_3_out, not_4_out);
  and and_12 (and_12_out, state[1], not_2_out, downcount);
  and and_13 (and_13_out, state[2], not_2_out, downcount);
  and and_14 (and_14_out, state[2], state[1], state[0], not_4_out);
  or or_1 (outstate[2], and_1_out, and_2_out, and_3_out, and_4_out);
  or or_2 (outstate[1], and_5_out, and_6_out, and_7_out, and_8_out, and_9_out);
  or or_3 (outstate[0], and_10_out, and_11_out, and_12_out, and_13_out, and_14_out);
endmodule
