// Logisim project Vending.circ as structural Verilog: 3 circuits, main circuit implementation
module implementation (
  input  EnableIn,
  input  QuarterReceivedIn,
  input  DimeReceivedIn,
  input  NickelReceivedIn,
  input  ClkIn,
  output Give_Mechandise_Out,
  output Give_Dime_Out,
  output Give_Nickel_Out
);

  wire [1:0] vendingcode;
  wire [3:0] register_1_q, state_1_stateout;

  or or_1 (Give_Mechandise_Out, vendingcode[0], vendingcode[1], Give_Dime_Out);
  or or_2 (Give_Nickel_Out, vendingcode[1], Give_Dime_Out);
  // Probe on register_1_q
  // Probe on state_1_stateout
  Register #(.width(4)) register_1 (.D(state_1_stateout), .en(EnableIn), .clk(ClkIn), .Q(register_1_q));  // open: clr
  state state_1 (
    .state(register_1_q), .coinrec({NickelReceivedIn, DimeReceivedIn, QuarterReceivedIn}),
    .stateout(state_1_stateout));
  howmuchchange howmuchchange_1 (
    .state(register_1_q), .coininput({NickelReceivedIn, DimeReceivedIn, QuarterReceivedIn}),
    .whattodispense({Give_Dime_Out, vendingcode}));
  // Probe on {Give_Dime_Out, vendingcode}

  // Other names for the same wires on the sheet: clk = ClkIn;
  //   coinrecieved[2:0] = {NickelReceivedIn, DimeReceivedIn, QuarterReceivedIn}; QuarterReceieved = QuarterReceivedIn;
  //   DimeReceieved = DimeReceivedIn; NickelReceieved = NickelReceivedIn; Enable = EnableIn;
  //   Give_Merchandise = Give_Mechandise_Out; Give_Nickel = Give_Nickel_Out; Give_Dime = Give_Dime_Out;
  //   vendingcode[2] = Give_Dime_Out
endmodule

module state (
  input  [3:0] state,
  input  [2:0] coinrec,
  output [3:0] stateout
);

  wire and_1_out, and_2_out, and_3_out, and_4_out, and_5_out, and_6_out, and_7_out, and_8_out, and_9_out,
       and_10_out, and_11_out, and_12_out, and_13_out, and_14_out, and_15_out, and_16_out, and_17_out,
       and_18_out, and_19_out, and_20_out, and_21_out, and_22_out, and_23_out, and_24_out, and_25_out,
       and_26_out, and_27_out, and_28_out, and_29_out, and_30_out, and_31_out, and_32_out, and_33_out,
       and_34_out, and_35_out, and_36_out, and_37_out, and_38_out, and_39_out, not_1_out, not_2_out,
       not_3_out, not_4_out, not_5_out, not_6_out, not_7_out;

  not not_1 (not_1_out, state[3]);
  not not_2 (not_2_out, state[2]);
  not not_3 (not_3_out, state[1]);
  not not_4 (not_4_out, state[0]);
  not not_5 (not_5_out, coinrec[2]);
  not not_6 (not_6_out, coinrec[1]);
  not not_7 (not_7_out, coinrec[0]);
  and and_1 (and_1_out, not_1_out, not_3_out, state[0], not_5_out, not_6_out, coinrec[0]);
  and and_2 (and_2_out, state[3], state[1]);
  and and_3 (and_3_out, state[3], state[2]);
  and and_4 (and_4_out, not_1_out, not_3_out, state[0], not_5_out, coinrec[1], not_7_out);
  and and_5 (and_5_out, not_1_out, not_2_out, not_3_out, state[0], coinrec[2], not_6_out, not_7_out);
  and and_6 (and_6_out, not_1_out, not_2_out, state[1], not_5_out, not_6_out, coinrec[0]);
  and and_7 (and_7_out, not_1_out, not_2_out, state[1], not_5_out, coinrec[1], not_7_out);
  and and_8 (and_8_out, not_1_out, not_2_out, state[1], not_4_out, coinrec[2], not_6_out, not_7_out);
  and and_9 (and_9_out, state[2], not_3_out, not_4_out, not_6_out);
  and and_10 (and_10_out, state[2], not_3_out, not_5_out, not_6_out, not_7_out);
  and and_11 (and_11_out, state[2], not_3_out, not_4_out, coinrec[0]);
  and and_12 (and_12_out, state[2], not_3_out, not_4_out, coinrec[2]);
  and and_13 (and_13_out, state[2], not_3_out, coinrec[2], coinrec[0]);
  and and_14 (and_14_out, state[2], not_3_out, state[0], coinrec[1]);
  and and_15 (and_15_out, state[3], state[2]);
  and and_16 (and_16_out, not_1_out, not_2_out, not_3_out, not_5_out, coinrec[1], not_7_out);
  and and_17 (and_17_out, not_1_out, not_2_out, not_3_out, coinrec[2], not_6_out, not_7_out);
  and and_18 (and_18_out, not_1_out, not_3_out, state[0], not_5_out, coinrec[1], not_7_out);
  and and_19 (and_19_out, not_2_out, state[1], not_5_out, not_6_out);
  and and_20 (and_20_out, not_2_out, state[1], coinrec[0]);
  and and_21 (and_21_out, not_2_out, state[1], coinrec[2], coinrec[1]);
  and and_22 (and_22_out, not_2_out, state[1], state[0], not_6_out);
  and and_23 (and_23_out, not_1_out, state[2], not_3_out, not_4_out, not_5_out, not_6_out, coinrec[0]);
  and and_24 (and_24_out, state[3], state[1]);
  and and_25 (and_25_out, not_1_out, not_2_out, not_4_out, not_5_out, not_6_out, coinrec[0]);
  and and_26 (and_26_out, not_1_out, not_3_out, not_5_out, not_6_out, coinrec[0]);
  and and_27 (and_27_out, not_1_out, not_3_out, not_4_out, coinrec[2], not_6_out, not_7_out);
  and and_28 (and_28_out, not_1_out, not_2_out, not_3_out, state[0], not_5_out);
  and and_29 (and_29_out, not_1_out, not_2_out, state[0], not_5_out, not_6_out, not_7_out);
  and and_30 (and_30_out, not_1_out, not_3_out, state[0], coinrec[0]);
  and and_31 (and_31_out, not_1_out, not_2_out, state[0], coinrec[1], coinrec[0]);
  and and_32 (and_32_out, not_1_out, not_2_out, state[0], coinrec[2], coinrec[0]);
  and and_33 (and_33_out, not_1_out, not_2_out, state[0], coinrec[2], coinrec[1]);
  and and_34 (and_34_out, not_1_out, not_2_out, state[1], not_4_out, not_5_out, coinrec[1], not_7_out);
  and and_35 (and_35_out, not_1_out, state[2], not_3_out, not_4_out, not_5_out, coinrec[1], not_7_out);
  and and_36 (and_36_out, state[2], not_3_out, state[0], not_6_out);
  and and_37 (and_37_out, state[2], not_3_out, state[0], coinrec[2]);
  and and_38 (and_38_out, state[3], state[1], state[0]);
  and and_39 (and_39_out, state[3], state[2], state[0]);
  or or_1 (stateout[3], and_1_out, and_2_out, and_3_out);
  or or_2 (stateout[1], and_16_out, and_17_out, and_18_out, and_19_out, and_20_out, and_21_out, and_22_out, and_23_out, and_24_out);
  or or_3 (stateout[2], and_4_out, and_5_out, and_6_out, and_7_out, and_8_out, and_9_out, and_10_out, and_11_out, and_12_out, and_13_out, and_14_out, and_15_out);
  or or_4 (stateout[0], and_25_out, and_26_out, and_27_out, and_28_out, and_29_out, and_30_out, and_31_out, and_32_out, and_33_out, and_34_out, and_35_out, and_36_out, and_37_out, and_38_out, and_39_out);
endmodule

module howmuchchange (
  input  [3:0] state,
  input  [2:0] coininput,
  output [2:0] whattodispense
);

  wire and_2_out, and_3_out, and_4_out, and_5_out, and_6_out, not_1_out, not_2_out, not_3_out, not_4_out,
       not_5_out, not_6_out, not_7_out;

  not not_1 (not_1_out, state[3]);
  not not_2 (not_2_out, state[2]);
  not not_3 (not_3_out, state[1]);
  not not_4 (not_4_out, state[0]);
  not not_5 (not_5_out, coininput[2]);
  not not_6 (not_6_out, coininput[1]);
  not not_7 (not_7_out, coininput[0]);
  and and_1 (whattodispense[2], not_1_out, not_3_out, state[0], not_5_out, not_6_out, coininput[0]);
  and and_2 (and_2_out, not_1_out, not_2_out, not_3_out, state[0], not_5_out, coininput[1], not_7_out);
  and and_3 (and_3_out, not_1_out, not_2_out, state[1], not_4_out, not_5_out, not_6_out, coininput[0]);
  and and_4 (and_4_out, not_1_out, not_2_out, not_3_out, state[0], coininput[2], not_6_out, not_7_out);
  and and_5 (and_5_out, not_1_out, not_2_out, state[1], state[0], not_5_out, not_6_out, coininput[0]);
  and and_6 (and_6_out, not_1_out, state[2], not_3_out, state[0], not_5_out, coininput[1], not_7_out);
  or or_1 (whattodispense[1], and_2_out, and_3_out);
  or or_2 (whattodispense[0], and_4_out, and_5_out, and_6_out);
endmodule
